// Logisim project Bresenham.circ as structural Verilog: 4 circuits, main circuit main
module main (
  input  [3:0] x0,
  input  [3:0] y0,
  input  [3:0] x1,
  input  [3:0] y1,
  input  Enable,
  input  Reset
);

  wire CLK, comparator_1_eq, comparator_2_eq, D_0, d_ff_2_q, d_ff_3_q, dcon, not_1_out, not_2_out, not_3_out,
       R, STOP;
  wire [3:0] adder_1_out, adder_2_out, multiplexer_1_out, multiplexer_2_out, multiplexer_3_out,
       multiplexer_4_out, register_1_q, register_2_q, shifter_1_out, shifter_2_out, subtractor_1_out,
       subtractor_2_out;
  wire [4:0] adder_3_out, adder_4_out, multiplexer_5_out, multiplexer_6_out, register_3_q, subtractor_3_out,
       subtractor_4_out;
  wire [14:0] b2ohd_1_out_2, demultiplexer_1_out0, demultiplexer_1_out1, demultiplexer_1_out2,
       demultiplexer_1_out3, demultiplexer_1_out4, demultiplexer_1_out5, demultiplexer_1_out6,
       demultiplexer_1_out7, demultiplexer_1_out8, demultiplexer_1_out9, demultiplexer_1_out10,
       demultiplexer_1_out11, demultiplexer_1_out12, demultiplexer_1_out13, demultiplexer_1_out14,
       demultiplexer_1_out15, fb_1_out_20, fb_1_out_21, fb_1_out_22, fb_1_out_23, fb_1_out_24, fb_1_out_25,
       fb_1_out_26, fb_1_out_27, fb_1_out_28, fb_1_out_29, fb_1_out_30, fb_1_out_31, fb_1_out_32,
       fb_1_out_33, fb_1_out_34, fb_1_out_35;
  wire [15:0] demultiplexer_2_out0;

  Adder #(.width(4)) adder_1 (.a(multiplexer_3_out), .b(4'b0001), .out(adder_1_out));  // open: cin, cout
  not not_1 (not_1_out, dcon);
  or or_1 (R, Reset, ~d_ff_3_q);  // OR_Gate
  Subtractor #(.width(4)) subtractor_1 (.a(y1), .b(y0), .out(subtractor_1_out));  // open: bin, bout
  Subtractor #(.width(4)) subtractor_2 (.a(x1), .b(x0), .out(subtractor_2_out));  // open: bin, bout
  not not_2 (not_2_out, dcon);
  Multiplexer #(.width(4)) multiplexer_1 (
    .in0(register_1_q), .in1(y0), .out(multiplexer_1_out), .sel(not_2_out));  // open: en
  Multiplexer #(.width(4)) multiplexer_2 (
    .in0(multiplexer_1_out), .in1(adder_1_out), .out(multiplexer_2_out), .sel(D_0));  // open: en
  Adder #(.width(4)) adder_2 (.a(multiplexer_4_out), .b(4'b0001), .out(adder_2_out));  // open: cin, cout
  D_Flip_Flop d_ff_1 (.clk(CLK), .D(not_1_out), .Q(dcon), .en(not_1_out), .reset(R));  // open: Qn, preset
  Clock clock_1 (.out(CLK));
  D_Flip_Flop d_ff_2 (.clk(CLK), .D(STOP), .Q(d_ff_2_q));  // open: Qn, preset, en, reset
  Register #(.width(4)) register_1 (.D(multiplexer_2_out), .en(not_3_out), .Q(register_1_q), .clk(CLK), .clr(R));
  Register #(.width(4)) register_2 (.D(adder_2_out), .en(STOP), .Q(register_2_q), .clk(CLK), .clr(R));
  D_Flip_Flop d_ff_3 (.clk(CLK), .D(d_ff_2_q), .Q(d_ff_3_q));  // open: Qn, preset, en, reset
  Shifter #(.width(4)) shifter_1 (.in(subtractor_1_out), .\dist (2'b01), .out(shifter_1_out));
  Shifter #(.width(4)) shifter_2 (.in(subtractor_2_out), .\dist (2'b01), .out(shifter_2_out));
  Comparator #(.width(4)) comparator_1 (.a(register_1_q), .b(y1), .eq(comparator_1_eq));  // open: gt, lt
  not not_3 (not_3_out, comparator_1_eq);
  Comparator #(.width(4)) comparator_2 (.a(register_2_q), .b(x1), .eq(comparator_2_eq));  // open: gt, lt
  not not_4 (STOP, comparator_2_eq);
  Multiplexer #(.width(4)) multiplexer_3 (
    .in0(y0), .in1(register_1_q), .out(multiplexer_3_out), .sel(dcon));  // open: en
  Multiplexer #(.width(4)) multiplexer_4 (
    .in0(x0), .in1(register_2_q), .out(multiplexer_4_out), .sel(dcon));  // open: en
  Subtractor #(.width(5)) subtractor_3 (
    .a({1'b0, shifter_1_out}), .b({1'b0, subtractor_2_out}), .out(subtractor_3_out));  // open: bin, bout
  Subtractor #(.width(5)) subtractor_4 (
    .a(multiplexer_6_out), .b({1'b0, shifter_2_out}), .out(subtractor_4_out));  // open: bin, bout
  Adder #(.width(5)) adder_3 (.a({1'b0, shifter_1_out}), .b(multiplexer_6_out), .out(adder_3_out));  // open: cin, cout
  Adder #(.width(5)) adder_4 (.a({1'b0, shifter_1_out}), .b(subtractor_4_out), .out(adder_4_out));  // open: cin, cout
  Multiplexer #(.width(5)) multiplexer_5 (
    .in0(adder_3_out), .in1(adder_4_out), .out(multiplexer_5_out), .sel(D_0));  // open: en
  Register #(.width(5)) register_3 (.D(multiplexer_5_out), .en(STOP), .Q(register_3_q), .clk(CLK), .clr(R));
  B2OHD b2ohd_1 (.in_1(multiplexer_4_out), .out_2(b2ohd_1_out_2));
  Demultiplexer #(.select(4), .width(15)) demultiplexer_1 (
    .out0(demultiplexer_1_out0), .out1(demultiplexer_1_out1), .out2(demultiplexer_1_out2),
    .out3(demultiplexer_1_out3), .out4(demultiplexer_1_out4), .out5(demultiplexer_1_out5),
    .out6(demultiplexer_1_out6), .out7(demultiplexer_1_out7), .out8(demultiplexer_1_out8),
    .out9(demultiplexer_1_out9), .out10(demultiplexer_1_out10), .out11(demultiplexer_1_out11),
    .out12(demultiplexer_1_out12), .out13(demultiplexer_1_out13), .out14(demultiplexer_1_out14),
    .out15(demultiplexer_1_out15), .in(b2ohd_1_out_2), .sel(multiplexer_3_out));  // open: en
  Demultiplexer #(.select(4)) demultiplexer_2 (
    .out0(demultiplexer_2_out0[0]), .out1(demultiplexer_2_out0[1]), .out2(demultiplexer_2_out0[2]),
    .out3(demultiplexer_2_out0[3]), .out4(demultiplexer_2_out0[4]), .out5(demultiplexer_2_out0[5]),
    .out6(demultiplexer_2_out0[6]), .out7(demultiplexer_2_out0[7]), .out8(demultiplexer_2_out0[8]),
    .out9(demultiplexer_2_out0[9]), .out10(demultiplexer_2_out0[10]), .out11(demultiplexer_2_out0[11]),
    .out12(demultiplexer_2_out0[12]), .out13(demultiplexer_2_out0[13]), .out14(demultiplexer_2_out0[14]),
    .out15(demultiplexer_2_out0[15]), .in(Enable), .sel(multiplexer_3_out));  // open: en
  Multiplexer #(.width(5)) multiplexer_6 (
    .in0(subtractor_3_out), .in1(register_3_q), .out(multiplexer_6_out), .sel(dcon));  // open: en
  FB fb_1 (
    .in_1(CLK), .in_2(R), .in_3(demultiplexer_2_out0), .in_4(demultiplexer_1_out0),
    .in_5(demultiplexer_1_out1), .in_6(demultiplexer_1_out2), .in_7(demultiplexer_1_out3),
    .in_8(demultiplexer_1_out4), .in_9(demultiplexer_1_out5), .in_10(demultiplexer_1_out6),
    .in_11(demultiplexer_1_out7), .in_12(demultiplexer_1_out8), .in_13(demultiplexer_1_out9),
    .in_14(demultiplexer_1_out10), .in_15(demultiplexer_1_out11), .in_16(demultiplexer_1_out12),
    .in_17(demultiplexer_1_out13), .in_18(demultiplexer_1_out14), .in_19(demultiplexer_1_out15),
    .out_20(fb_1_out_20), .out_21(fb_1_out_21), .out_22(fb_1_out_22), .out_23(fb_1_out_23),
    .out_24(fb_1_out_24), .out_25(fb_1_out_25), .out_26(fb_1_out_26), .out_27(fb_1_out_27),
    .out_28(fb_1_out_28), .out_29(fb_1_out_29), .out_30(fb_1_out_30), .out_31(fb_1_out_31),
    .out_32(fb_1_out_32), .out_33(fb_1_out_33), .out_34(fb_1_out_34), .out_35(fb_1_out_35));
  DotMatrix #(.inputtype("row"), .matrixcols(15), .matrixrows(16)) dotmatrix_1 (
    .row0(fb_1_out_20), .row1(fb_1_out_21), .row2(fb_1_out_22), .row3(fb_1_out_23), .row4(fb_1_out_24),
    .row5(fb_1_out_25), .row6(fb_1_out_26), .row7(fb_1_out_27), .row8(fb_1_out_28), .row9(fb_1_out_29),
    .row10(fb_1_out_30), .row11(fb_1_out_31), .row12(fb_1_out_32), .row13(fb_1_out_33), .row14(fb_1_out_34),
    .row15(fb_1_out_35));
  Comparator #(.width(5)) comparator_3 (.a(multiplexer_6_out), .b({5{1'b0}}), .gt(D_0));  // open: eq, lt

  // Other names for the same wires on the sheet: E = Enable; xcon = dcon; ycon = dcon

  // Notes on the sheet:
  //   dy
  //   dx
  //   y
  //   x
  //   Usage:
  //   Set Enable to one
  //   Enter the points
  //   Coordinates are 4 bit unsigned integers
  //   x1 and y1 must be bigger than x0 and y0
  //   The Circuit draws the line over and over again
  //   Bresenham's Line Algorithm
  //   plotLine(x0, y0, x1, y1)
  //   dx = x1 - x0
  //   dy = y1 - y0
  //   D = 2*dy-dx
  //   y = y0
  //   end if
  //   for x from x0 to x1
  //   plot(x,y)
  //   if(D > 0)
  //   y = y + 1
  //   D = D - 2*dx
  //   D = D + 2*dy
  //   15
  //   x=0
  //   15
  //   y=0
endmodule

module ABS (
  input  [3:0] in_1,
  output [3:0] out_2
);

  wire [3:0] xor_1_out;

  assign xor_1_out = {4{in_1[3]}} ^ in_1;  // XOR_Gate xor_1, 4 bits wide
  Adder #(.width(4)) adder_1 (.a(xor_1_out), .b({3'b000, in_1[3]}), .out(out_2));  // open: cin, cout
endmodule

module FB (
  input  in_1,
  input  in_2,
  input  [15:0] in_3,
  input  [14:0] in_4,
  input  [14:0] in_5,
  input  [14:0] in_6,
  input  [14:0] in_7,
  input  [14:0] in_8,
  input  [14:0] in_9,
  input  [14:0] in_10,
  input  [14:0] in_11,
  input  [14:0] in_12,
  input  [14:0] in_13,
  input  [14:0] in_14,
  input  [14:0] in_15,
  input  [14:0] in_16,
  input  [14:0] in_17,
  input  [14:0] in_18,
  input  [14:0] in_19,
  output [14:0] out_20,
  output [14:0] out_21,
  output [14:0] out_22,
  output [14:0] out_23,
  output [14:0] out_24,
  output [14:0] out_25,
  output [14:0] out_26,
  output [14:0] out_27,
  output [14:0] out_28,
  output [14:0] out_29,
  output [14:0] out_30,
  output [14:0] out_31,
  output [14:0] out_32,
  output [14:0] out_33,
  output [14:0] out_34,
  output [14:0] out_35
);

  wire [14:0] or_1_out, or_2_out, or_3_out, or_4_out, or_5_out, or_6_out, or_7_out, or_8_out, or_9_out,
       or_10_out, or_11_out, or_12_out, or_13_out, or_14_out, or_15_out, or_16_out;

  assign or_1_out = out_20 | in_4;  // OR_Gate or_1, 15 bits wide
  assign or_2_out = out_21 | in_5;  // OR_Gate or_2, 15 bits wide
  assign or_3_out = out_22 | in_6;  // OR_Gate or_3, 15 bits wide
  assign or_4_out = out_23 | in_7;  // OR_Gate or_4, 15 bits wide
  assign or_5_out = out_24 | in_8;  // OR_Gate or_5, 15 bits wide
  assign or_6_out = out_25 | in_9;  // OR_Gate or_6, 15 bits wide
  assign or_7_out = out_26 | in_10;  // OR_Gate or_7, 15 bits wide
  assign or_8_out = out_27 | in_11;  // OR_Gate or_8, 15 bits wide
  assign or_9_out = out_28 | in_12;  // OR_Gate or_9, 15 bits wide
  assign or_10_out = out_29 | in_13;  // OR_Gate or_10, 15 bits wide
  assign or_11_out = out_30 | in_14;  // OR_Gate or_11, 15 bits wide
  assign or_12_out = out_31 | in_15;  // OR_Gate or_12, 15 bits wide
  assign or_13_out = out_32 | in_16;  // OR_Gate or_13, 15 bits wide
  assign or_14_out = out_33 | in_17;  // OR_Gate or_14, 15 bits wide
  assign or_15_out = out_34 | in_18;  // OR_Gate or_15, 15 bits wide
  assign or_16_out = out_35 | in_19;  // OR_Gate or_16, 15 bits wide
  Register #(.width(15)) register_1 (.D(or_1_out), .en(in_3[0]), .Q(out_20), .clk(in_1), .clr(in_2));
  Register #(.width(15)) register_2 (.D(or_2_out), .en(in_3[1]), .Q(out_21), .clk(in_1), .clr(in_2));
  Register #(.width(15)) register_3 (.D(or_3_out), .en(in_3[2]), .Q(out_22), .clk(in_1), .clr(in_2));
  Register #(.width(15)) register_4 (.D(or_4_out), .en(in_3[3]), .Q(out_23), .clk(in_1), .clr(in_2));
  Register #(.width(15)) register_5 (.D(or_5_out), .en(in_3[4]), .Q(out_24), .clk(in_1), .clr(in_2));
  Register #(.width(15)) register_6 (.D(or_6_out), .en(in_3[5]), .Q(out_25), .clk(in_1), .clr(in_2));
  Register #(.width(15)) register_7 (.D(or_7_out), .en(in_3[6]), .Q(out_26), .clk(in_1), .clr(in_2));
  Register #(.width(15)) register_8 (.D(or_8_out), .en(in_3[7]), .Q(out_27), .clk(in_1), .clr(in_2));
  Register #(.width(15)) register_9 (.D(or_9_out), .en(in_3[8]), .Q(out_28), .clk(in_1), .clr(in_2));
  Register #(.width(15)) register_10 (.D(or_10_out), .en(in_3[9]), .Q(out_29), .clk(in_1), .clr(in_2));
  Register #(.width(15)) register_11 (.D(or_11_out), .en(in_3[10]), .Q(out_30), .clk(in_1), .clr(in_2));
  Register #(.width(15)) register_12 (.D(or_12_out), .en(in_3[11]), .Q(out_31), .clk(in_1), .clr(in_2));
  Register #(.width(15)) register_13 (.D(or_13_out), .en(in_3[12]), .Q(out_32), .clk(in_1), .clr(in_2));
  Register #(.width(15)) register_14 (.D(or_14_out), .en(in_3[13]), .Q(out_33), .clk(in_1), .clr(in_2));
  Register #(.width(15)) register_15 (.D(or_15_out), .en(in_3[14]), .Q(out_34), .clk(in_1), .clr(in_2));
  Register #(.width(15)) register_16 (.D(or_16_out), .en(in_3[15]), .Q(out_35), .clk(in_1), .clr(in_2));

  // Other names for the same wires on the sheet: CLK = in_1; E[15:0] = in_3; R = in_2
endmodule

module B2OHD (
  input  [3:0] in_1,
  output [14:0] out_2
);

  wire and_16_out, not_1_out, not_2_out, not_3_out, not_4_out;

  not not_1 (not_1_out, in_1[3]);
  not not_2 (not_2_out, in_1[0]);
  not not_3 (not_3_out, in_1[1]);
  not not_4 (not_4_out, in_1[2]);
  and and_1 (out_2[0], not_1_out, not_4_out, not_3_out, not_2_out);
  and and_2 (out_2[1], in_1[0], not_3_out, not_4_out, not_1_out);
  and and_3 (out_2[2], not_2_out, in_1[1], not_4_out, not_1_out);
  and and_4 (out_2[3], in_1[0], in_1[1], not_4_out, not_1_out);
  and and_5 (out_2[4], not_2_out, not_3_out, in_1[2], not_1_out);
  and and_6 (out_2[5], in_1[0], not_3_out, in_1[2], not_1_out);
  and and_7 (out_2[6], not_2_out, in_1[1], in_1[2], not_1_out);
  and and_8 (out_2[7], in_1[0], in_1[1], in_1[2], not_1_out);
  and and_9 (out_2[8], not_2_out, not_3_out, not_4_out, in_1[3]);
  and and_10 (out_2[9], in_1[0], not_3_out, not_4_out, in_1[3]);
  and and_11 (out_2[10], not_2_out, in_1[1], not_4_out, in_1[3]);
  and and_12 (out_2[11], in_1[0], in_1[1], in_1[3], not_4_out);
  and and_13 (out_2[12], not_2_out, not_3_out, in_1[2], in_1[3]);
  and and_14 (out_2[13], in_1[0], not_3_out, in_1[2], in_1[3]);
  and and_15 (out_2[14], not_2_out, in_1[1], in_1[2], in_1[3]);
  and and_16 (and_16_out, in_1[0], in_1[1], in_1[2], in_1[3]);
endmodule
